# Fritzing sketch telecommande (saved by Fritzing 0.9.3b)
breadboards: 2

parts:
  BAT1 = Battery Holders [package=lipo-1100mAh]
  Composant1 = TFT 1.8 inch 160x128 w microSD [part_number=358]  # not connected
  S1-R = Momentary Switch [package=ksa_sealed_tac_switch]
  S2-G = Momentary Switch [package=ksa_sealed_tac_switch]
  S3-Y = Momentary Switch [package=ksa_sealed_tac_switch]
  S4-B = Momentary Switch [package=ksa_sealed_tac_switch]
  ENCODER1 = Rotary Encoder with Knob
  S1 = Momentary Switch [package=ksa_sealed_tac_switch]
  R5 = Resistor [tolerance=±1% resistance=22 package=THT]
  R6 = Resistor [tolerance=±1% resistance=22 package=THT]
  R7 = Resistor [tolerance=±1% resistance=22 package=THT]
  LED1 = RGB LED - (4 legs) [package="5 mm [THT]"]
  MCU2 = Wemos D32 pro
  J1-secousse = male pin header, 3 pins [form="♂ (male)"]

nets:
  N1: BAT1.+, MCU2.pin_17
  N2: BAT1.-, S1-R.3, S2-G.3, S3-Y.3, S4-B.3, ENCODER1.no_name_yet#4, S1.3, MCU2.pin_18, MCU2.pin_19, MCU2.pin_34, J1-secousse.pin2
  N3: S1-R.1, MCU2.pin_6
  N4: S2-G.1, MCU2.pin_7
  N5: S3-Y.1, MCU2.pin_8
  N6: S4-B.1, MCU2.pin_9
  N7: ENCODER1.no_name_yet#5, MCU2.pin_22
  N8: S1.1, MCU2.pin_13
  N9: R5.Pin_0, LED1.red_cathode
  N10: R5.Pin_1, MCU2.pin_10
  N11: R6.Pin_0, LED1.green_cathode
  N12: R6.Pin_1, MCU2.pin_11
  N13: R7.Pin_0, LED1.blue_cathode
  N14: R7.Pin_1, MCU2.pin_12
  N15: LED1.common_anode, MCU2.pin_1, J1-secousse.pin3
  N16: MCU2.pin_5, J1-secousse.pin1

custom parts:
  TFT 1.8 inch 160x128 w microSD: This lovely little display breakout is the best way to add a small, colorful and bright display to any project. Since the display uses 4-wire SPI to communicate and has its own pixel-addressable frame buffer, it can be used with every kind of microcontroller. Even a very small one with low memory and few pins available! The 1.8" display has 128x160 color pixels.
  Rotary Encoder with Knob: Rotary Encoder with 1/4" Shaft and Knob
  Wemos D32 pro: Wemos D32 pro wifi and blue tooth board based on the ESP-32 cpu, digital I/Os 22, analog inputs 6, analog outputs 2, clock 240mhz, Flash 4Mbytes, PSRAM 4MB, microSD card slot, lipo battery charger (500ma connection broken out on breadboard but not pcb), usb.
